# Fritzing sketch Led_Inspection (saved by Fritzing 0.9.3b)
breadboards: 1

parts:
  Part1 = Arduino Uno (Rev3)
  R1 = Resistor [tolerance=±5% resistance=220 package=THT]
  LED1 = LED - 5mm [color="Red (633nm)" package="5 mm [THT]"]

nets:
  N1: Part1.A0, R1.Pin_1
  N2: Part1.A5/SCL, R1.Pin_0, LED1.anode
  N3: Part1.GND, LED1.cathode
